# Fritzing sketch OneWireKeyPad-3buttons (saved by Fritzing 0.9.4)
circuit board: 4.29213cm x 1.5842cm
breadboards: 1

parts:
  J2 = male pin header, 3 pins [form="♂ (male)"]
  R5 = Resistor [tolerance=±5% resistance=4.7k package=THT]
  R6 = Resistor [tolerance=±5% resistance=4.7k package=THT]
  R7 = Resistor [tolerance=±5% resistance=4.7k package=THT]
  R8 = Resistor [tolerance=±5% resistance=1.1k package=THT]
  J1 = male pin header, 4 pins [form="♂ (male)"]

nets:
  N1: J2.pin1, R8.Pin_1, J1.pin1
  N2: J2.pin2, R6.Pin_0, R7.Pin_1, J1.pin4
  N3: J2.pin3, R7.Pin_0
  N4: R5.Pin_0, R6.Pin_1, J1.pin3
  N5: R5.Pin_1, R8.Pin_0, J1.pin2

notes:
  3-button One Wire Keypad
  5V
  GND
  Out
  Y
  G
  R
  G-Y-R
