# Fritzing sketch OneWireKeyPad (saved by Fritzing 0.9.3b)
circuit board: 4.46192cm x 2.40319cm
breadboards: 1

parts:
  J1 = male pin header, 7 pins [form="♂ (male)"]
  J2 = male pin header, 3 pins [form="♂ (male)"]
  R1 = Resistor [tolerance=±5% resistance=470 package=THT]
  R2 = Resistor [tolerance=±5% resistance=470 package=THT]
  R3 = Resistor [tolerance=±5% resistance=4.7k package=THT]
  R5 = Resistor [tolerance=±5% resistance=1.1k package=THT]
  R6 = Resistor [tolerance=±5% resistance=1.1k package=THT]
  R7 = Resistor [tolerance=±5% resistance=1.1k package=THT]

nets:
  N1: J1.pin1, J2.pin1, R1.Pin_1
  N2: J1.pin2, R1.Pin_0, R2.Pin_1
  N3: J1.pin3, R2.Pin_0, R3.Pin_1
  N4: J1.pin4, R3.Pin_0
  N5: J1.pin5, R5.Pin_1
  N6: J1.pin6, R5.Pin_0, R6.Pin_1
  N7: J1.pin7, J2.pin2, R6.Pin_0, R7.Pin_1
  N8: J2.pin3, R7.Pin_0

notes:
  One Wire Keypad 3C X 4R
  5V
  GND
  Out
  R1
  R2
  R3
  C1
  C2
  C3
  R4
